// Digital circuit decoder.dig as structural Verilog
module decoder (
  input  A,
  input  B,
  input  C,
  input  D,
  output sign,
  output a_2,
  output d_2,
  output b_2,
  output c_2,
  output e,
  output f,
  output g
);

  wire and_1_out, and_3_out, and_4_out, and_5_out, and_6_out, and_7_out, and_8_out, not_1_out, not_2_out,
       not_3_out;

  not not_1 (not_1_out, A);
  not not_2 (not_2_out, B);
  not not_3 (not_3_out, C);
  or or_1 (c_2, not_2_out, A);
  and and_1 (and_1_out, A, C, not_2_out);
  and and_2 (f, not_1_out, not_2_out);
  and and_3 (and_3_out, not_1_out, C);
  and and_4 (and_4_out, not_2_out, C);
  and and_5 (and_5_out, B, not_3_out);
  and and_6 (and_6_out, not_1_out, B);
  and and_7 (and_7_out, not_1_out, not_3_out);
  or or_2 (g, and_3_out, and_4_out, and_5_out);
  and and_8 (and_8_out, not_1_out, B);
  or or_3 (e, and_7_out, and_8_out);
  or or_4 (a_2, and_1_out, and_5_out, and_6_out, and_7_out);

  assign b_2 = 1'b1;
  assign d_2 = a_2;
  assign sign = C;
endmodule
