// Digital circuit lab2_10_component.dig as structural Verilog
module lab2_10_component (
  input  in_1,
  input  in_2,
  input  in_3,
  input  in_4
);

  wire _74248_1_pin9, _74248_1_pin10, _74248_1_pin11, _74248_1_pin12, _74248_1_pin13, _74248_1_pin14,
       _74248_1_pin15, dipswitch_1_out, dipswitch_2_out, dipswitch_3_out, dipswitch_4_out, sub_1_c_o,
       sub_1_s, sub_2_c_o, sub_2_s, sub_3_c_o, sub_3_s, sub_4_s;

  DipSwitch #(.dipDefault("true")) dipswitch_1 (.out(dipswitch_1_out));
  DipSwitch dipswitch_2 (.out(dipswitch_2_out));
  DipSwitch #(.dipDefault("true")) dipswitch_3 (.out(dipswitch_3_out));
  DipSwitch dipswitch_4 (.out(dipswitch_4_out));
  Sub sub_1 (.a(dipswitch_4_out), .b(in_1), .c_i(1'b0), .s(sub_1_s), .c_o(sub_1_c_o));
  Sub sub_2 (.a(dipswitch_3_out), .b(in_2), .c_i(sub_1_c_o), .s(sub_2_s), .c_o(sub_2_c_o));
  Sub sub_3 (.a(dipswitch_2_out), .b(in_3), .c_i(sub_2_c_o), .s(sub_3_s), .c_o(sub_3_c_o));
  Sub sub_4 (.a(dipswitch_1_out), .b(in_4), .c_i(sub_3_c_o), .s(sub_4_s));  // open: c_o
  _74248 _74248_1 (
    .pin1(sub_2_s), .pin2(sub_3_s), .pin3(1'b1), .pin4(1'b1), .pin5(1'b1), .pin6(sub_4_s), .pin7(sub_1_s),
    .pin8(1'b0), .pin9(_74248_1_pin9), .pin10(_74248_1_pin10), .pin11(_74248_1_pin11),
    .pin12(_74248_1_pin12), .pin13(_74248_1_pin13), .pin14(_74248_1_pin14), .pin15(_74248_1_pin15),
    .pin16(1'b1));
  Seven_Seg seven_seg_1 (
    .a(_74248_1_pin13), .b(_74248_1_pin12), .c(_74248_1_pin11), .d(_74248_1_pin10), .e(_74248_1_pin9),
    .f(_74248_1_pin15), .g(_74248_1_pin14), .dp(1'b0));
endmodule
