// Digital circuit prelab2.dig as structural Verilog
module prelab2 (
  input  X0,
  input  X1,
  input  X2,
  input  Y0,
  input  Y1,
  input  Y2,
  output A,
  output B,
  output C,
  output D,
  output E,
  output F,
  output G,
  output Sign
);

  wire add_1_c_o, add_1_s, add_2_c_o, add_2_s, add_3_c_o, add_3_s;

  Add add_1 (.a(X2), .b(Y2), .c_i(1'b0), .s(add_1_s), .c_o(add_1_c_o));
  Add add_2 (.a(X1), .b(Y1), .c_i(add_1_c_o), .s(add_2_s), .c_o(add_2_c_o));
  Add add_3 (.a(X0), .b(Y0), .c_i(add_2_c_o), .s(add_3_s), .c_o(add_3_c_o));
  decoder decoder_1 (
    .A(add_1_s), .B(add_2_s), .C(add_3_s), .D(add_3_c_o), .sign(Sign), .a_2(A), .d_2(D), .b_2(B), .c_2(C),
    .e(E), .f(F), .g(G));
endmodule
